# Fritzing sketch pulse-generator (saved by Fritzing 0.9.9b)
breadboards: 1

parts:
  Part1 = Arduino Uno (Rev3)
  R3 = TRIMPOT [package=3386u]
  R4 = Resistor [tolerance=±5% power=0.25 resistance=220 package=THT]
  LED1 = LED - 5mm [color="Red (633nm)" current=0.030 package="5 mm [THT]"]

nets:
  N1: Part1.A0, R3.WIPER
  N2: Part1.D11_PWM/MOSI, R4.Pin_0, R4.Pin_1, LED1.anode
  N3: Part1.GND, R3.CCW, LED1.cathode
  N4: Part1.5V, R3.CW
